# Fritzing sketch Beacons (saved by Fritzing 0.9.0b)
circuit board: 7cm x 5cm
breadboards: 1

parts:
  Part1 = Arduino Pro Mini v13
  Q1 = npn-Powertransistor [part_number=BC237 package="TO220 [THT]"]
  R1 = Resistor [tolerance=±5% resistance=4.7 package=THT]
  R2 = Resistor [tolerance=±5% resistance=1k package=THT]
  D1 = LTE-302 [package=lte-302]
  D2 = LTE-302 [package=lte-302]
  12v = Battery block 12V
  C1 = Electrolytic Capacitor [capacitance=10µF package="100 mil [THT, electrolytic]"]
  C2 = Electrolytic Capacitor [capacitance=10µF package="100 mil [THT, electrolytic]"]
  U1 = Voltage Regulator - 5V [package="TO220 [THT]"]

nets:
  GND: Part1.GND, Q1.emitter, 12v.-, C1.-, C2.-, U1.GND
  N1: Part1.RAW, 12v.+, C1.+, U1.input_voltage
  N2: Part1.D3_PWM, R2.Pin_1
  N3: Q1.base, R2.Pin_0
  N4: Q1.collector, D1.C
  N5: R1.Pin_0, C2.+, U1.output_voltage
  N6: R1.Pin_1, D2.A
  N7: D1.A, D2.C

notes:
  Voltage Regulator For LEDs
  Two IR LEDs controlled by an NPN Transistor
  Ranch Racing Lap Timer, IR Beacon For Vehicle
  12V Not 9v
  Any Voltage From 7-14 will work

custom parts:
  Battery block 12V: Your standard 12 Volts battery block
