# Fritzing sketch RRMainBoardNew (saved by Fritzing 0.9.0b)
circuit board: 10cm x 7cm
breadboards: 1

parts:
  Mega2560 = Arduino Mega 2560 (Rev3)
  BATTERY = Battery Holders [package=battcom_20mm_pth]
  txrxgn_vcgn = Thermal Printer
  DS1302 = DS1302 [package="DIP8 [THT]"]
  rs3_3 = female pin header, 2 pins [form="♀ (female)"]
  gn = female pin header, 2 pins [form="♀ (female)"]
  momi = female pin header, 2 pins [form="♀ (female)"]
  R1 = Resistor [tolerance=±5% resistance=1.5k package=THT]
  R2 = Resistor [tolerance=±5% resistance=1.5k package=THT]
  Crystal = CRYSTAL [package=tc38h]
  sdsc = female pin header, 2 pins [form="♀ (female)"]
  SCLSDA = Header 2 [package=molex-1x2_lock]
  Vin = Header 2 [package=molex-1x2_lock]
  GN/5v = Header 2 [package=molex-1x2_lock]
  txRx2txRx1 = female pin header, 4 pins [form="♀ (female)"]
  TXRX3 = female pin header, 2 pins [form="♀ (female)"]
  RYGVCC = female pin header, 4 pins [form="♀ (female)"]

nets:
  A0: Mega2560.A0, RYGVCC.pin1
  N1: Mega2560.A1, RYGVCC.pin2
  A2: Mega2560.A2, RYGVCC.pin3
  SCL: Mega2560.D21/SCL, Mega2560.SCL, R1.Pin_0, SCLSDA.2
  SDA: Mega2560.D20/SDA, Mega2560.SDA, R2.Pin_0, SCLSDA.1
  N2: Mega2560.D19/RX1, txRx2txRx1.pin4
  N3: Mega2560.D18/TX1, txRx2txRx1.pin3
  N4: Mega2560.D17_PWM/RX2, txRx2txRx1.pin2
  N5: Mega2560.D16_PWM/TX2, txRx2txRx1.pin1
  N6: Mega2560.D15/RX3, TXRX3.pin2
  N7: Mega2560.D14/TX3, TXRX3.pin1
  GND: Mega2560.GND, BATTERY.-, txrxgn_vcgn.GND, DS1302.0V, gn.pin1, Vin.1, GN/5v.1
  N8: Mega2560.D13_PWM, txrxgn_vcgn.RXD
  SCLK: Mega2560.D12_PWM, DS1302.SCLK_-_SPI_Clock
  I/O: Mega2560.D11_PWM, DS1302.I/O_-_SPI_Data_In/Out
  CE: Mega2560.D10_PWM, DS1302.CE_-_Chip_Enable
  N9: Mega2560.D9_PWM, rs3_3.pin2
  3 Volts: Mega2560.3V3, rs3_3.pin1
  5 Volts: Mega2560.5V, DS1302.+V, R1.Pin_1, R2.Pin_1, GN/5v.2, RYGVCC.pin4
  N10: Mega2560.VIN, txrxgn_vcgn.VH, Vin.2
  N11: Mega2560.D7_PWM, txrxgn_vcgn.TXD
  N12: Mega2560.D50, momi.pin1
  N13: Mega2560.D51, momi.pin2
  N14: Mega2560.D52, sdsc.pin1
  N15: Mega2560.D53, sdsc.pin2
  N16: BATTERY.+, DS1302.Vbat_-_Backup_Supply
  N17: DS1302.X1_-_Crystal, Crystal.2
  N18: DS1302.X2_-_Crystal, Crystal.1

notes:
  Ranch Racing
  Lap Timer Main Unit
  V1.01
