# Fritzing sketch ranchRacingReceiver (saved by Fritzing 0.9.0b)
circuit board: 7cm x 9cm
breadboards: 1

parts:
  Part1 = Arduino Pro Mini v13
  IR1 = TSOP312.., 314.. [package=THT]
  TXRX5vGn = female pin header, 4 pins [form="♀ (female)"]
  SDASCL = female pin header, 2 pins [form="♀ (female)"]

nets:
  N1: Part1.VCC, IR1.Vs, TXRX5vGn.pin3
  GND: Part1.GND, IR1.GND, TXRX5vGn.pin4
  N2: Part1.A4, SDASCL.pin2
  N3: Part1.A5, SDASCL.pin1
  N4: Part1.D2, IR1.Data
  N5: Part1.D1/RX, TXRX5vGn.pin2
  N6: Part1.D0/TX, TXRX5vGn.pin1

notes:
  IR Receiver 1.03
