# Fritzing sketch tvoutrr (saved by Fritzing 0.9.0b)
circuit board: 3.1cm x 4.5cm
breadboards: 1

parts:
  ProMini5v = Arduino Pro Mini v13
  R1 = Resistor [tolerance=±5% resistance=1k package=THT]
  R2 = Resistor [tolerance=±5% resistance=470 package=THT]
  Vin/GN/Rx/Tx = female pin header, 4 pins [form="♀ (female)"]
  V/Gn/Au = female pin header, 3 pins [form="♀ (female)"]

nets:
  VoltageInRAW: ProMini5v.RAW, Vin/GN/Rx/Tx.pin1
  GND: ProMini5v.GND, Vin/GN/Rx/Tx.pin2, V/Gn/Au.pin2
  D11: ProMini5v.D11_PWM/MOSI, V/Gn/Au.pin3
  N1: ProMini5v.D9_PWM, R1.Pin_0
  N2: ProMini5v.D7, R2.Pin_0
  N3: ProMini5v.D1/RX, Vin/GN/Rx/Tx.pin3
  N4: ProMini5v.D0/TX, Vin/GN/Rx/Tx.pin4
  N5: R1.Pin_1, R2.Pin_1, V/Gn/Au.pin1

notes:
  TVOut
  Ranch Racing
  Video Ground Audio
  Vin Ground RX TX
